// Digital circuit ALUProiectFIC.dig as structural Verilog
// Arithmetic Logical unit.
// Performs all arithmetic operations.
// Used for arithmetic processor instructions as well as for 
// calculating memory addresses.
// {{de Arithmetisch Logische Einheit. 
// Führt alle arithmetischen Operationen durch. 
// Wird sowohl für arithmetische Prozessorbefehle 
// als auch für die Berechnung der Adressen 
// bei der Speicheradressierung verwendet.}}
module ALUProiectFIC (
  input  [15:0] A,
  input  [15:0] B,
  input  [4:0] Op,
  input  clk,
  output [15:0] Y,
  output Zero,
  output Neg,
  output Carry,
  output UsgALU,
  output Overflow,
  output UsgALU_plus
);

  wire add_1_c_o, comparator_1_eq, comparator_2_eq, comparator_3_eq, comparator_4_eq, comparator_5_eq,
       DEC_c_o, decoder_1_out_9, decoder_1_out_10, decoder_1_out_11, decoder_1_out_12, decoder_1_out_13,
       decoder_1_out_14, decoder_1_out_15, decoder_1_out_16, decoder_1_out_17, decoder_1_out_18,
       decoder_1_out_19, decoder_1_out_20, decoder_1_out_21, decoder_1_out_22, decoder_1_out_23,
       decoder_1_out_24, decoder_1_out_25, decoder_1_out_29, INC_c_o, or_2_out, ovrflwAdd, ovrflwDec,
       ovrflwInc, ovrflwSubCmp, powOp, sub_1_c_o;
  wire [15:0] add_1_s, and_1_out, DEC_s, div_1_q, div_1_r, INC_s, LSL_out, LSR_out, not_1_out, or_1_out,
       powRes, RSL_out, RSR_out, sub_1_s, xor_1_out;
  wire [31:0] mul_1_mul;

  PowerOp powerop_1 (.A(A), .clk(clk), .B(B), .powOp(powOp), .ResToALU(powRes));
  Comparator #(.Bits(5)) comparator_1 (.a(Op), .b(5'b01001), .eq(comparator_1_eq));  // open: gt, lt
  Add #(.Bits(16)) add_1 (.a(A), .b(B), .c_i(1'b0), .s(add_1_s), .c_o(add_1_c_o));
  Sub #(.Bits(16)) sub_1 (.a(A), .b(B), .c_i(1'b0), .s(sub_1_s), .c_o(sub_1_c_o));
  BarrelShifter #(.Bits(16), .direction("right")) LSR (.in(A), .shift(B[4:0]), .out(LSR_out));
  BarrelShifter #(.Bits(16)) LSL (.in(A), .shift(B[4:0]), .out(LSL_out));
  BarrelShifter #(.Bits(16), .barrelShifterMode("rotate"), .direction("right")) RSR (
    .in(A), .shift(B[4:0]), .out(RSR_out));
  BarrelShifter #(.Bits(16), .barrelShifterMode("rotate")) RSL (.in(A), .shift(B[4:0]), .out(RSL_out));
  Mul #(.Bits(16)) mul_1 (.a(A), .b(B), .mul(mul_1_mul));
  Div #(.Bits(16)) div_1 (.a(A), .b(B), .q(div_1_q), .r(div_1_r));
  assign and_1_out = A & B;  // And and_1, 16 bits wide
  assign or_1_out = A | B;  // Or or_1, 16 bits wide
  assign xor_1_out = A ^ B;  // XOr xor_1, 16 bits wide
  assign not_1_out = ~A;  // Not not_1, 16 bits wide
  Add #(.Bits(16)) INC (.a(A), .b(16'h1), .c_i(1'b0), .s(INC_s), .c_o(INC_c_o));
  Sub #(.Bits(16)) DEC (.a(A), .b(16'h1), .c_i(1'b0), .s(DEC_s), .c_o(DEC_c_o));
  Comparator #(.Bits(5)) comparator_2 (.a(Op), .b(5'b10111), .eq(comparator_2_eq));  // open: gt, lt
  and and_2 (ovrflwAdd, comparator_1_eq, add_1_c_o);
  and and_3 (ovrflwInc, INC_c_o, comparator_2_eq);
  Comparator #(.Bits(5)) comparator_3 (.a(Op), .b(5'b01010), .eq(comparator_3_eq));  // open: gt, lt
  Comparator #(.Bits(5)) comparator_4 (.a(Op), .b(5'b11001), .eq(comparator_4_eq));  // open: gt, lt
  or or_2 (or_2_out, comparator_3_eq, comparator_4_eq);
  Multiplexer #(.Selector_Bits(5), .Bits(16)) multiplexer_1 (
    .sel(Op), .in_0(B), .in_1(A), .in_2(B), .in_3(B), .in_4(B), .in_5(B), .in_6(B), .in_7(B), .in_8(B),
    .in_9(add_1_s), .in_10(sub_1_s), .in_11(LSR_out), .in_12(LSL_out), .in_13(RSR_out), .in_14(RSL_out),
    .in_15(mul_1_mul[15:0]), .in_16(div_1_q), .in_17(div_1_r), .in_18(and_1_out), .in_19(or_1_out),
    .in_20(xor_1_out), .in_21(B), .in_22(not_1_out), .in_23(INC_s), .in_24(DEC_s), .in_25(sub_1_s),
    .in_26(powRes), .in_27({16{1'b0}}), .in_28({16{1'b0}}), .in_29(powRes), .in_30({16{1'b0}}),
    .in_31({16{1'b0}}), .out(Y));
  LookUpTable u_CARRY (
    .in0(Op[0]), .in1(Op[1]), .in2(add_1_c_o), .in3(sub_1_c_o), .in4(INC_c_o), .in5(DEC_c_o), .out(Carry));
  Decoder #(.Selector_Bits(5)) decoder_1 (
    .sel(Op), .out_9(decoder_1_out_9), .out_10(decoder_1_out_10), .out_11(decoder_1_out_11),
    .out_12(decoder_1_out_12), .out_13(decoder_1_out_13), .out_14(decoder_1_out_14),
    .out_15(decoder_1_out_15), .out_16(decoder_1_out_16), .out_17(decoder_1_out_17),
    .out_18(decoder_1_out_18), .out_19(decoder_1_out_19), .out_20(decoder_1_out_20),
    .out_21(decoder_1_out_21), .out_22(decoder_1_out_22), .out_23(decoder_1_out_23),
    .out_24(decoder_1_out_24), .out_25(decoder_1_out_25), .out_26(powOp), .out_29(decoder_1_out_29));  // open: out_0, out_1, out_2, out_3, out_4, out_5, out_6, out_7, out_8, out_27, out_28, out_30, out_31
  Comparator #(.Bits(5)) comparator_5 (.a(Op), .b(5'b11000), .eq(comparator_5_eq));  // open: gt, lt
  and and_4 (ovrflwSubCmp, or_2_out, sub_1_c_o);
  and and_5 (ovrflwDec, DEC_c_o, comparator_5_eq);
  Comparator #(.Signed("true"), .Bits(16)) comparator_6 (.a(Y), .b({16{1'b0}}), .eq(Zero), .lt(Neg));  // open: gt
  or or_3 (UsgALU, decoder_1_out_9, decoder_1_out_10, decoder_1_out_11, decoder_1_out_12, decoder_1_out_13, decoder_1_out_14, decoder_1_out_15, decoder_1_out_16, decoder_1_out_17, decoder_1_out_18, decoder_1_out_19, decoder_1_out_20, decoder_1_out_21, decoder_1_out_22, decoder_1_out_23, decoder_1_out_24);
  or or_4 (Overflow, ovrflwAdd, ovrflwSubCmp, ovrflwInc, ovrflwDec);
  or or_5 (UsgALU_plus, UsgALU, decoder_1_out_25, powOp, decoder_1_out_29);

  // Other names for the same wires on the sheet: sel[4:0] = Op

  // Notes on the sheet:
  //   A: first operand
  //   B: second operand
  //   Op: opCode
  //   Y: result
  //   Zero: Zero-flag. Is high if the relult is zero.
  //   {{de Zero-Flag; Ist High wenn das Ergebnis Null ist.}}
  //   Neg: Is high if the result is negative.
  //   {{de Ist High wenn das Ergebnis negativ ist.}}
  //   Carry: Is high if there has been a carry.
  //   {{de Ist High wenn es einen Übertrag gegeben hat.}}
  //   contents of CARRY (hex, n*v repeats v):
  //   5*0,1,4*0,1,0,0,1,1,4*0,1,0,1,0,1,0,0,1,1,0,4*1,0,0,0,1,1,0,0
  //   ,1,0,1,0,1,1,1,0,1,0,0,1,1,1,0,1,1,0,6*1
endmodule
