// Digital circuit ControlUnit.dig as structural Verilog
module ControlUnit (
  input  [4:0] OpCode,
  input  [1:0] MCmp,
  input  MLoad,
  input  MStore,
  input  MALU,
  input  MMov,
  input  ZEROFLAG,
  input  NEG,
  input  CARRY,
  input  OVERFLOW,
  input  usageALU,
  input  [15:0] PCval,
  input  MPow,
  input  nopWE,
  output M,
  output zero,
  output [15:0] one,
  output loadOp,
  output retOp,
  output jmpOp,
  output stackOp,
  output selPC,
  output writeRegisterFile,
  output strDM,
  output [15:0] zero16b,
  output HLT,
  output StartSP,
  output enSP,
  output Imm1,
  output Imm2,
  output NOP
);

  wire aluOp, and_1_out, and_2_out, and_3_out, and_4_out, and_5_out, and_6_out, and_7_out, and_8_out,
       branchOp, cmp1imm, cmpImmediate1, cmpImmediate2, cmpOp, cmpPrimImm, comparator_1_eq, comparator_2_eq,
       comparator_3_eq, comparator_4_eq, comparator_5_eq, decoder_1_out_2, decoder_1_out_3, decoder_1_out_4,
       decoder_1_out_5, decoder_1_out_6, decoder_1_out_7, decoder_1_out_8, decoder_1_out_9, decoder_1_out_10,
       decoder_1_out_11, decoder_1_out_12, decoder_1_out_13, decoder_1_out_14, decoder_1_out_15,
       decoder_1_out_16, decoder_1_out_17, decoder_1_out_18, decoder_1_out_19, decoder_1_out_20, decOp,
       incOp, mdlOp, movOp, notOp, powImm1, powOp, storeOp;

  Decoder #(.Selector_Bits(5)) decoder_1 (
    .sel(OpCode), .out_0(loadOp), .out_1(storeOp), .out_2(decoder_1_out_2), .out_3(decoder_1_out_3),
    .out_4(decoder_1_out_4), .out_5(decoder_1_out_5), .out_6(decoder_1_out_6), .out_7(decoder_1_out_7),
    .out_8(decoder_1_out_8), .out_9(decoder_1_out_9), .out_10(decoder_1_out_10), .out_11(decoder_1_out_11),
    .out_12(decoder_1_out_12), .out_13(decoder_1_out_13), .out_14(decoder_1_out_14),
    .out_15(decoder_1_out_15), .out_16(decoder_1_out_16), .out_17(decoder_1_out_17),
    .out_18(decoder_1_out_18), .out_19(decoder_1_out_19), .out_20(decoder_1_out_20), .out_21(movOp),
    .out_22(notOp), .out_23(incOp), .out_24(decOp), .out_25(cmpOp), .out_26(powOp), .out_27(mdlOp),
    .out_28(HLT), .out_29(NOP));  // open: out_30, out_31
  Comparator #(.Bits(5)) comparator_1 (.a(OpCode), .b(5'b00010), .eq(comparator_1_eq));  // open: gt, lt
  Comparator #(.Bits(5)) comparator_2 (.a(OpCode), .b(5'b00011), .eq(comparator_2_eq));  // open: gt, lt
  Comparator #(.Bits(5)) comparator_3 (.a(OpCode), .b(5'b00100), .eq(comparator_3_eq));  // open: gt, lt
  Comparator #(.Bits(5)) comparator_4 (.a(OpCode), .b(5'b00101), .eq(comparator_4_eq));  // open: gt, lt
  Comparator #(.Bits(5)) comparator_5 (.a(OpCode), .b(5'b00110), .eq(comparator_5_eq));  // open: gt, lt
  Comparator #(.Bits(5)) comparator_6 (.a(OpCode), .b(5'b00111), .eq(jmpOp));  // open: gt, lt
  Comparator #(.Bits(5)) comparator_7 (.a(OpCode), .b(5'b01000), .eq(retOp));  // open: gt, lt
  Comparator #(.Bits(16)) comparator_8 (.a(PCval), .b(16'h1), .eq(StartSP));  // open: gt, lt
  or or_1 (branchOp, decoder_1_out_2, decoder_1_out_3, decoder_1_out_4, decoder_1_out_5, decoder_1_out_6, decoder_1_out_7, decoder_1_out_8);
  or or_2 (aluOp, decoder_1_out_9, decoder_1_out_10, decoder_1_out_11, decoder_1_out_12, decoder_1_out_13, decoder_1_out_14, decoder_1_out_15, decoder_1_out_16, decoder_1_out_17, decoder_1_out_18, decoder_1_out_19, decoder_1_out_20);
  or or_3 (enSP, stackOp, StartSP);
  and and_1 (and_1_out, ZEROFLAG, 1'b1);
  and and_2 (and_2_out, NEG, 1'b1);
  and and_3 (and_3_out, CARRY, 1'b1);
  and and_4 (and_4_out, OVERFLOW, 1'b1);
  and and_5 (and_5_out, comparator_1_eq, and_1_out);
  and and_6 (and_6_out, comparator_2_eq, and_2_out);
  and and_7 (and_7_out, comparator_3_eq, and_3_out);
  and and_8 (and_8_out, comparator_4_eq, and_4_out);
  Comparator #(.Bits(2)) comparator_9 (.a(MCmp), .b(2'b11), .eq(cmpImmediate2));  // open: gt, lt
  Comparator #(.Bits(2)) comparator_10 (.a(MCmp), .b(2'b01), .eq(cmpPrimImm));  // open: gt, lt
  Comparator #(.Bits(2)) comparator_11 (.a(MCmp), .b(2'b10), .eq(cmp1imm));  // open: gt, lt
  or or_4 (stackOp, jmpOp, retOp);
  or or_5 (selPC, and_5_out, and_6_out, and_7_out, and_8_out, comparator_5_eq, jmpOp, retOp);
  or or_6 (M, MLoad, MStore, cmp1imm, branchOp, MALU, MMov);
  or or_7 (cmpImmediate1, cmpPrimImm, cmpImmediate2);
  or or_8 (writeRegisterFile, loadOp, nopWE, usageALU);
  or or_9 (strDM, jmpOp, storeOp);
  and and_9 (powImm1, MPow, 1'b1);
  or or_10 (Imm1, cmpImmediate1, mdlOp, powImm1);
  or or_11 (Imm2, cmpImmediate2, powOp);

  assign one = 16'h1;
  assign zero = 1'b0;
  assign zero16b = {16{1'b0}};
endmodule
