// Digital circuit FlagsRegisterFileProiectFic.dig as structural Verilog
module FlagsRegisterFileProiectFic (
  input  zero,
  input  C,
  input  negative,
  input  carry,
  input  overfl,
  output ZEROFLAG,
  output NEG,
  output CARRYFLAG,
  output OVERFLOW
);

  Register u_ZERO (.D(zero), .C(C), .en(1'b1), .Q(ZEROFLAG));
  Register u_NEG (.D(negative), .C(C), .en(1'b1), .Q(NEG));
  Register u_CARRY (.D(carry), .C(C), .en(1'b1), .Q(CARRYFLAG));
  Register u_OVERFLOW (.D(overfl), .C(C), .en(1'b1), .Q(OVERFLOW));
endmodule
