// Digital circuit InstructionDecoderProiectFIC.dig as structural Verilog
module InstructionDecoderProiectFIC (
  input  [15:0] Instruction,
  output [1:0] RD,
  output [10:0] SgnExt,
  output [1:0] RS2,
  output [1:0] RS1,
  output [10:0] SignExt2,
  output MLoad,
  output MALU,
  output MStore,
  output MMov,
  output [1:0] MCmp,
  output [4:0] OpCode,
  output MPow,
  output nopWE
);

  wire [1:0] demultiplexer_2_out_0, demultiplexer_5_out_0, demultiplexer_6_out_0, demultiplexer_6_out_0_3,
       demultiplexer_6_out_1, demultiplexer_6_out_2_2, demultiplexer_7_out_0, or_2_out_2;
  wire [3:0] demultiplexer_6_out_2, demultiplexer_6_out_3;
  wire [3:2] demultiplexer_6_out_1_2;
  wire [4:0] demultiplexer_2_out_1, demultiplexer_6_out_1_3;
  wire [4:2] demultiplexer_2_out_0_2;
  wire [5:0] demultiplexer_4_out_0, demultiplexer_4_out_1;
  wire [7:0] demultiplexer_3_out_0, demultiplexer_3_out_1, demultiplexer_5_out_1, demultiplexer_7_out_1;
  wire [7:2] demultiplexer_5_out_0_2, demultiplexer_7_out_0_2;
  wire [8:0] demultiplexer_1_out_25;
  wire [8:2] demultiplexer_6_out_0_2;
  wire [8:4] demultiplexer_6_out_3_2;
  wire [8:6] demultiplexer_6_out_2_3;
  wire [9:0] demultiplexer_1_out_0, demultiplexer_1_out_1, demultiplexer_1_out_21, demultiplexer_1_out_26,
       or_2_out;
  wire [10:0] demultiplexer_1_out_2, demultiplexer_1_out_3, demultiplexer_1_out_4, demultiplexer_1_out_5,
       demultiplexer_1_out_6, demultiplexer_1_out_7, demultiplexer_1_out_8, demultiplexer_1_out_9,
       demultiplexer_1_out_10, demultiplexer_1_out_11, demultiplexer_1_out_12, demultiplexer_1_out_13,
       demultiplexer_1_out_14, demultiplexer_1_out_15, demultiplexer_1_out_16, demultiplexer_1_out_17,
       demultiplexer_1_out_18, demultiplexer_1_out_19, demultiplexer_1_out_20, demultiplexer_1_out_22,
       demultiplexer_1_out_23, demultiplexer_1_out_24, demultiplexer_1_out_27, or_1_out;
  wire [10:1] demultiplexer_1_out_29;

  Demultiplexer #(.Selector_Bits(5), .Bits(11)) demultiplexer_1 (
    .sel(Instruction[15:11]), .in(Instruction[10:0]), .out_0({MLoad, demultiplexer_1_out_0}),
    .out_1({MStore, demultiplexer_1_out_1}), .out_2(demultiplexer_1_out_2), .out_3(demultiplexer_1_out_3),
    .out_4(demultiplexer_1_out_4), .out_5(demultiplexer_1_out_5), .out_6(demultiplexer_1_out_6),
    .out_7(demultiplexer_1_out_7), .out_8(demultiplexer_1_out_8), .out_9(demultiplexer_1_out_9),
    .out_10(demultiplexer_1_out_10), .out_11(demultiplexer_1_out_11), .out_12(demultiplexer_1_out_12),
    .out_13(demultiplexer_1_out_13), .out_14(demultiplexer_1_out_14), .out_15(demultiplexer_1_out_15),
    .out_16(demultiplexer_1_out_16), .out_17(demultiplexer_1_out_17), .out_18(demultiplexer_1_out_18),
    .out_19(demultiplexer_1_out_19), .out_20(demultiplexer_1_out_20),
    .out_21({MMov, demultiplexer_1_out_21}), .out_22(demultiplexer_1_out_22),
    .out_23(demultiplexer_1_out_23), .out_24(demultiplexer_1_out_24),
    .out_25({MCmp, demultiplexer_1_out_25}), .out_26({MPow, demultiplexer_1_out_26}),
    .out_27(demultiplexer_1_out_27), .out_29({demultiplexer_1_out_29, nopWE}));  // open: out_28, out_30, out_31
  assign or_1_out = demultiplexer_1_out_2 | demultiplexer_1_out_3 | demultiplexer_1_out_4 | demultiplexer_1_out_5 | demultiplexer_1_out_6 | demultiplexer_1_out_7 | demultiplexer_1_out_8;  // Or or_1, 11 bits wide
  assign {MALU, or_2_out[9:8], or_2_out_2, or_2_out[5:0]} = demultiplexer_1_out_9 | demultiplexer_1_out_10 | demultiplexer_1_out_11 | demultiplexer_1_out_12 | demultiplexer_1_out_13 | demultiplexer_1_out_14 | demultiplexer_1_out_15 | demultiplexer_1_out_16 | demultiplexer_1_out_17 | demultiplexer_1_out_18 | demultiplexer_1_out_19 | demultiplexer_1_out_20;  // Or or_2, 11 bits wide
  Demultiplexer #(.Bits(5)) demultiplexer_2 (
    .sel(MPow), .in(demultiplexer_1_out_26[9:5]), .out_0({demultiplexer_2_out_0_2, demultiplexer_2_out_0}),
    .out_1(demultiplexer_2_out_1));
  Demultiplexer #(.Bits(8)) demultiplexer_3 (
    .sel(MLoad), .in(demultiplexer_1_out_0[7:0]), .out_0(demultiplexer_3_out_0), .out_1(demultiplexer_3_out_1));
  Demultiplexer #(.Bits(6)) demultiplexer_4 (
    .sel(MALU), .in(or_2_out[5:0]), .out_0(demultiplexer_4_out_0), .out_1(demultiplexer_4_out_1));
  Demultiplexer #(.Bits(8)) demultiplexer_5 (
    .sel(MMov), .in(demultiplexer_1_out_21[7:0]), .out_0({demultiplexer_5_out_0_2, demultiplexer_5_out_0}),
    .out_1(demultiplexer_5_out_1));
  Demultiplexer #(.Selector_Bits(2), .Bits(9)) demultiplexer_6 (
    .sel(MCmp), .in(demultiplexer_1_out_25),
    .out_0({demultiplexer_6_out_0_2[8:6], demultiplexer_6_out_0_3, demultiplexer_6_out_0_2[3:2], demultiplexer_6_out_0}),
    .out_1({demultiplexer_6_out_1_3, demultiplexer_6_out_1_2, demultiplexer_6_out_1}),
    .out_2({demultiplexer_6_out_2_3, demultiplexer_6_out_2_2, demultiplexer_6_out_2}),
    .out_3({demultiplexer_6_out_3_2, demultiplexer_6_out_3}));
  Demultiplexer #(.Bits(8)) demultiplexer_7 (
    .sel(MStore), .in(demultiplexer_1_out_1[9:2]), .out_0({demultiplexer_7_out_0_2, demultiplexer_7_out_0}),
    .out_1(demultiplexer_7_out_1));
  assign RS1 = demultiplexer_3_out_0[1:0] | demultiplexer_7_out_0 | or_2_out_2 | demultiplexer_5_out_0;  // Or or_3, 2 bits wide
  assign RS2 = demultiplexer_4_out_0[1:0] | demultiplexer_6_out_0 | demultiplexer_6_out_1;  // Or or_4, 2 bits wide
  assign RD = demultiplexer_1_out_0[9:8] | demultiplexer_1_out_1[1:0] | demultiplexer_6_out_0_3 | or_2_out[9:8] | demultiplexer_1_out_21[9:8] | demultiplexer_1_out_29[2:1] | demultiplexer_1_out_22[1:0] | demultiplexer_1_out_23[1:0] | demultiplexer_1_out_24[1:0] | demultiplexer_6_out_2_2 | demultiplexer_2_out_0;  // Or or_5, 2 bits wide
  assign SgnExt = {3'b000, demultiplexer_3_out_1} | {3'b000, demultiplexer_7_out_1} | or_1_out | {{5{1'b0}}, demultiplexer_4_out_1} | {3'b000, demultiplexer_5_out_1} | {{6{1'b0}}, demultiplexer_6_out_1_3} | {{7{1'b0}}, demultiplexer_6_out_2} | {{6{1'b0}}, demultiplexer_6_out_3_2} | {1'b0, demultiplexer_1_out_27[9:0]} | {{6{1'b0}}, demultiplexer_2_out_1};  // Or or_6, 11 bits wide
  assign SignExt2 = {{7{1'b0}}, demultiplexer_6_out_3} | {{6{1'b0}}, demultiplexer_1_out_26[4:0]};  // Or or_7, 11 bits wide

  assign OpCode = Instruction[15:11];
endmodule
