// Digital circuit OperandsRegisterFileFIC.dig as structural Verilog
module OperandsRegisterFileFIC (
  input  clk,
  input  [4:0] OpC,
  input  [15:0] A,
  input  [15:0] B,
  output [15:0] Op1,
  output [15:0] Op2
);

  wire comparator_1_eq;

  Comparator #(.Bits(5)) comparator_1 (.a(OpC), .b(5'b11010), .eq(comparator_1_eq));  // open: gt, lt
  Register #(.Bits(16)) u_Op1 (.D(A), .C(clk), .en(comparator_1_eq), .Q(Op1));
  Register #(.Bits(16)) u_Op2 (.D(B), .C(clk), .en(comparator_1_eq), .Q(Op2));
endmodule
