// Digital circuit PowerOp.dig as structural Verilog
module PowerOp (
  input  [15:0] A,
  input  clk,
  input  [15:0] B,
  input  powOp,
  output [15:0] ResToALU
);

  wire comparator_2_eq, comparator_2_gt, exp0, or_1_out;
  wire [15:0] counterpreset_1_out, multiplexer_1_out, multiplexer_2_out, register_1_q;
  wire [31:0] mul_1_mul;

  Comparator #(.Bits(16)) comparator_1 (.a(B), .b({16{1'b0}}), .eq(exp0));  // open: gt, lt
  CounterPreset #(.Bits(16)) counterpreset_1 (
    .en(comparator_2_gt), .C(clk), .dir(1'b1), .in(B), .ld(powOp), .clr(1'b0), .out(counterpreset_1_out));  // open: ovf
  Multiplexer #(.Bits(16)) multiplexer_1 (
    .sel(comparator_2_gt), .in_0(16'h1), .in_1(register_1_q), .out(multiplexer_1_out));
  Mul #(.Bits(16)) mul_1 (.a(A), .b(multiplexer_1_out), .mul(mul_1_mul));
  Comparator #(.Bits(16)) comparator_2 (
    .a(counterpreset_1_out), .b(16'h1), .gt(comparator_2_gt), .eq(comparator_2_eq));  // open: lt
  Multiplexer #(.Bits(16)) multiplexer_2 (.sel(exp0), .in_0(register_1_q), .in_1(16'h1), .out(multiplexer_2_out));
  Register #(.Bits(16)) register_1 (.D(mul_1_mul[15:0]), .C(clk), .en(1'b1), .Q(register_1_q));
  or or_1 (or_1_out, comparator_2_eq, exp0);
  Multiplexer #(.Bits(16)) multiplexer_3 (.sel(or_1_out), .in_0({16{1'b0}}), .in_1(multiplexer_2_out), .out(ResToALU));
endmodule
