// Digital circuit ProcesorProiectFIC.dig as structural Verilog
// The processor.
// A circuit which combines multiple necessary modules, such as the
// Program Counter, the Instruction and Data Memories, the Control Unit,
// the Sign Extend Unit, the Register File, the ALU, the Flags Register and the
// Stack Pointer.
// This big circuit is resposible with fetching instructions (one by one) from the
// Instruction Memory, decode them, send the data through the correct buses,
// generating the control signals depeding on the binary information received
// from the 16-bit instructions, computing some operations inside the ALU and
// writing/reading results from three registers (X, Y, Accumulator).
// The processor is the heart of a computer, therefore it is responsible with
// every kind of calculations.
module ProcesorProiectFIC (
  input  clock
);

  wire ALU_carry, ALU_neg, ALU_overflow, ALU_usgalu_plus, ALU_zero, Carry, ControlUnit_writeregisterfile,
       enSP, HLT, Imm1, Imm2, InstructionDecoder_malu, InstructionDecoder_mload, InstructionDecoder_mmov,
       InstructionDecoder_mpow, InstructionDecoder_mstore, jmpOp, loadOp, M, multiplexer_5_out, Neg, nop,
       nopWE, not_1_out, not_2_out, Overflow, reset_out, retOp, selPC, stackOp, startSP, strDM, usageALU,
       zero, ZeroFlag;
  wire [1:0] InstructionDecoder_mcmp, InstructionDecoder_rd, InstructionDecoder_rs1, InstructionDecoder_rs2;
  wire [4:0] InstructionDecoder_opcode;
  wire [10:0] InstructionDecoder_sgnext, InstructionDecoder_signext2;
  wire [15:0] ALU_y, DM_d, IM_d, multiplexer_1_out, multiplexer_2_out, multiplexer_3_out, multiplexer_4_out,
       multiplexer_6_out, multiplexer_7_out, multiplexer_8_out, multiplexer_9_out, multiplexer_10_out,
       multiplexer_11_out, multiplexer_12_out, multiplexer_13_out, multiplexer_14_out, multiplexer_15_out,
       multiplexer_16_out, multiplexer_17_out, one, PC_q, PCval, PowOperandsRegisterFile_op1,
       PowOperandsRegisterFile_op2, RegisterFile_rdest, RegisterFile_rsrc1, RegisterFile_rsrc2,
       SignExtend_immediate1, SignExtend_immediate2, SP_1_s, SP_plus_1_s, SP_q, zero16b;

  Multiplexer #(.Bits(16)) multiplexer_1 (
    .sel(selPC), .in_0(PCval), .in_1(multiplexer_11_out), .out(multiplexer_1_out));
  Register #(.Bits(16), .isProgramCounter("true")) PC (.D(multiplexer_1_out), .C(clock), .en(reset_out), .Q(PC_q));
  Reset reset (.out(reset_out));
  Add #(.Bits(16)) PC_plus_1 (.a(PC_q), .b(one), .c_i(zero), .s(PCval));  // open: c_o
  not not_1 (not_1_out, HLT);
  RAMDualPort #(.AddrBits(16), .isProgramMemory("true"), .Bits(16)) IM (
    .A(PC_q), .Din(zero16b), .str(HLT), .C(clock), .ld(not_1_out), .D(IM_d));
  InstructionDecoderProiectFIC InstructionDecoder (
    .Instruction(IM_d), .RD(InstructionDecoder_rd), .SgnExt(InstructionDecoder_sgnext),
    .RS2(InstructionDecoder_rs2), .RS1(InstructionDecoder_rs1), .SignExt2(InstructionDecoder_signext2),
    .MLoad(InstructionDecoder_mload), .MALU(InstructionDecoder_malu), .MStore(InstructionDecoder_mstore),
    .MMov(InstructionDecoder_mmov), .MCmp(InstructionDecoder_mcmp), .OpCode(InstructionDecoder_opcode),
    .MPow(InstructionDecoder_mpow), .nopWE(nopWE));
  ControlUnit ControlUnit (
    .OpCode(InstructionDecoder_opcode), .MCmp(InstructionDecoder_mcmp), .MLoad(InstructionDecoder_mload),
    .MStore(InstructionDecoder_mstore), .MALU(InstructionDecoder_malu), .MMov(InstructionDecoder_mmov),
    .ZEROFLAG(ZeroFlag), .NEG(Neg), .CARRY(Carry), .OVERFLOW(Overflow), .usageALU(usageALU), .PCval(PCval),
    .MPow(InstructionDecoder_mpow), .nopWE(nopWE), .M(M), .zero(zero), .one(one), .loadOp(loadOp),
    .retOp(retOp), .jmpOp(jmpOp), .stackOp(stackOp), .selPC(selPC),
    .writeRegisterFile(ControlUnit_writeregisterfile), .strDM(strDM), .zero16b(zero16b), .HLT(HLT),
    .StartSP(startSP), .enSP(enSP), .Imm1(Imm1), .Imm2(Imm2), .NOP(nop));
  SignExtendUnit SignExtend (
    .SgnExt1(InstructionDecoder_sgnext), .SgnExt2(InstructionDecoder_signext2),
    .Immediate1(SignExtend_immediate1), .Immediate2(SignExtend_immediate2));
  Multiplexer #(.Bits(16)) multiplexer_2 (
    .sel(ALU_usgalu_plus), .in_0(SignExtend_immediate1), .in_1(ALU_y), .out(multiplexer_2_out));
  Multiplexer #(.Bits(16)) multiplexer_3 (.sel(loadOp), .in_0(multiplexer_2_out), .in_1(DM_d), .out(multiplexer_3_out));
  RegisterFileProiectFIC RegisterFile (
    .WD(multiplexer_3_out), .C(clock), .RS1(InstructionDecoder_rs1), .RD(InstructionDecoder_rd),
    .RS2(InstructionDecoder_rs2), .WE(ControlUnit_writeregisterfile), .Rdest(RegisterFile_rdest),
    .Rsrc1(RegisterFile_rsrc1), .Rsrc2(RegisterFile_rsrc2));
  Multiplexer #(.Bits(16)) multiplexer_4 (
    .sel(multiplexer_5_out), .in_0(RegisterFile_rsrc1), .in_1(RegisterFile_rsrc2), .out(multiplexer_4_out));
  Multiplexer multiplexer_5 (
    .sel(ALU_usgalu_plus), .in_0(InstructionDecoder_rs2[0]), .in_1(ALU_usgalu_plus), .out(multiplexer_5_out));
  Multiplexer #(.Bits(16)) multiplexer_6 (
    .sel(Imm1), .in_0(RegisterFile_rdest), .in_1(SignExtend_immediate1), .out(multiplexer_6_out));
  Multiplexer #(.Bits(16)) multiplexer_7 (
    .sel(M), .in_0(multiplexer_4_out), .in_1(SignExtend_immediate1), .out(multiplexer_7_out));
  OperandsRegisterFileFIC PowOperandsRegisterFile (
    .clk(clock), .OpC(InstructionDecoder_opcode), .A(multiplexer_6_out), .B(multiplexer_8_out),
    .Op1(PowOperandsRegisterFile_op1), .Op2(PowOperandsRegisterFile_op2));
  Multiplexer #(.Bits(16)) multiplexer_8 (
    .sel(Imm2), .in_0(multiplexer_7_out), .in_1(SignExtend_immediate2), .out(multiplexer_8_out));
  Multiplexer #(.Bits(16)) multiplexer_9 (
    .sel(nop), .in_0(multiplexer_6_out), .in_1(PowOperandsRegisterFile_op1), .out(multiplexer_9_out));
  Multiplexer #(.Bits(16)) multiplexer_10 (
    .sel(nop), .in_0(multiplexer_8_out), .in_1(PowOperandsRegisterFile_op2), .out(multiplexer_10_out));
  ALUProiectFIC ALU (
    .A(multiplexer_9_out), .B(multiplexer_10_out), .Op(InstructionDecoder_opcode), .clk(clock), .Y(ALU_y),
    .Zero(ALU_zero), .Neg(ALU_neg), .Carry(ALU_carry), .UsgALU(usageALU), .Overflow(ALU_overflow),
    .UsgALU_plus(ALU_usgalu_plus));
  Multiplexer #(.Bits(16)) multiplexer_11 (.sel(retOp), .in_0(ALU_y), .in_1(DM_d), .out(multiplexer_11_out));
  Multiplexer #(.Bits(16)) multiplexer_12 (
    .sel(jmpOp), .in_0(multiplexer_10_out), .in_1(PCval), .out(multiplexer_12_out));
  // FlagsRegisterFileProiectFic FlagsRegister: pin names not known; wires that end beside it: ALU_zero, clock, ALU_neg, ALU_carry, ALU_overflow, ZeroFlag, Neg, Carry, Overflow
  Multiplexer #(.Bits(16)) multiplexer_13 (
    .sel(stackOp), .in_0(ALU_y), .in_1(multiplexer_16_out), .out(multiplexer_13_out));
  not not_2 (not_2_out, strDM);
  RAMDualPort #(.AddrBits(16), .Bits(16)) DM (
    .A(multiplexer_13_out), .Din(multiplexer_12_out), .str(strDM), .C(clock), .ld(not_2_out), .D(DM_d));
  Multiplexer #(.Bits(16)) multiplexer_14 (.sel(retOp), .in_0(SP_1_s), .in_1(SP_plus_1_s), .out(multiplexer_14_out));
  Multiplexer #(.Bits(16)) multiplexer_15 (
    .sel(stackOp), .in_0(SP_q), .in_1(multiplexer_14_out), .out(multiplexer_15_out));
  Multiplexer #(.Bits(16)) multiplexer_16 (
    .sel(retOp), .in_0(SP_q), .in_1(multiplexer_17_out), .out(multiplexer_16_out));
  Multiplexer #(.Bits(16)) multiplexer_17 (
    .sel(startSP), .in_0(multiplexer_15_out), .in_1({16{1'b1}}), .out(multiplexer_17_out));
  Sub #(.Bits(16)) SP_1 (.a(SP_q), .b(one), .c_i(zero), .s(SP_1_s));  // open: c_o
  Register #(.Bits(16)) SP (.D(multiplexer_17_out), .C(clock), .en(enSP), .Q(SP_q));
  Add #(.Bits(16)) SP_plus_1 (.a(SP_q), .b(one), .c_i(zero), .s(SP_plus_1_s));  // open: c_o

  // Other names for the same wires on the sheet: clk = clock
endmodule
