// Digital circuit RegisterFileProiectFIC.dig as structural Verilog
// This block contains the 16 processor registers.
// {{de In diesem Block befinden sich die 16 
// Prozessorregister.}}
module RegisterFileProiectFIC (
  input  [15:0] WD,
  input  C,
  input  [1:0] RS1,
  input  [1:0] RD,
  input  [1:0] RS2,
  input  WE,
  output [15:0] Rdest,
  output [15:0] Rsrc1,
  output [15:0] Rsrc2
);

  wire demultiplexer_1_out_0, demultiplexer_1_out_1, demultiplexer_1_out_2;
  wire [15:0] Acc_q, X_q, Y_q;

  Demultiplexer #(.Selector_Bits(2)) demultiplexer_1 (
    .sel(RD), .in(WE), .out_0(demultiplexer_1_out_0), .out_1(demultiplexer_1_out_1),
    .out_2(demultiplexer_1_out_2));  // open: out_3
  Register #(.Bits(16)) X (.D(WD), .C(C), .en(demultiplexer_1_out_0), .Q(X_q));
  Register #(.Bits(16)) Y (.D(WD), .C(C), .en(demultiplexer_1_out_1), .Q(Y_q));
  Register #(.Bits(16)) Acc (.D(WD), .C(C), .en(demultiplexer_1_out_2), .Q(Acc_q));
  Multiplexer #(.Selector_Bits(2), .Bits(16)) multiplexer_1 (
    .sel(RD), .in_0(X_q), .in_1(Y_q), .in_2(Acc_q), .in_3({16{1'b0}}), .out(Rdest));
  Multiplexer #(.Selector_Bits(2), .Bits(16)) multiplexer_2 (
    .sel(RS1), .in_0(X_q), .in_1(Y_q), .in_2(Acc_q), .in_3({16{1'b0}}), .out(Rsrc1));
  Multiplexer #(.Selector_Bits(2), .Bits(16)) multiplexer_3 (
    .sel(RS2), .in_0(X_q), .in_1(Y_q), .in_2(Acc_q), .in_3({16{1'b0}}), .out(Rsrc2));

  // Notes on the sheet:
  //   WD: Data to be stored.
  //   The value applied here is stored when the input WE is set to 1.
  //   {{de Daten die gespeichert werden sollen.
  //   Der hier anliegende Wert wird gespeichert, wenn 
  //   der Eingang WE auf 1 geschaltet wird.}}
  //   RS1: Number of the source register. 
  //   Defines which register is to be output to Rsrc.
  //   {{de Nummer des Source Registers. Legt fest, welches 
  //   Register an Rsrc ausgegeben werden soll.}}
  //   Rdest: Contents of the Destignation Register.
  //   Which register is output is determined by 
  //   the input dest.
  //   {{de  Inhalt des Destignation Registers.
  //   Welches Register ausgegeben wird, wird mittels 
  //   des Eingangs dest festgelegt.}}
  //   Rsrc1: Contents of the Source Register.
  //   Which register is output is determined by the input src.
  //   {{de Inhalt des Source Registers. Welches Register
  //   ausgegeben wird, wird mittels des Einganges src
  //   festgelegt.}}
  //   RS2: Number of the source register. 
  //   Defines which register is to be output to Rsrc.
  //   {{de Nummer des Source Registers. Legt fest, welches 
  //   Register an Rsrc ausgegeben werden soll.}}
  //   Rsrc2: Contents of the Source Register.
  //   Which register is output is determined by the input src.
  //   {{de Inhalt des Source Registers. Welches Register
  //   ausgegeben wird, wird mittels des Einganges src
  //   festgelegt.}}
endmodule
