// Digital circuit SignExtendUnit.dig as structural Verilog
module SignExtendUnit (
  input  [10:0] SgnExt1,
  input  [10:0] SgnExt2,
  output [15:0] Immediate1,
  output [15:0] Immediate2
);


  assign Immediate1 = {{5{1'b0}}, SgnExt1};
  assign Immediate2 = {{5{1'b0}}, SgnExt2};
endmodule
